# Fritzing sketch project1 (saved by Fritzing 0.9.5d)
breadboards: 1

parts:
  A2 = Waveshare rp2040-zero tht extra conns [package=THT]
  Part1 = INA219 High Side DC Current Sensor Breakout [part_number=904]
  U1 = SBX DSUN [package=THT]  # not connected
  OLED2 = OLED 128x64 I2C Monochrome Display VDD-GND
  S1 = Pushbutton [package="[THT]"]
  S2 = Pushbutton [package="[THT]"]
  R1 = Trimmer Potentiometer [maximum_resistance=10kΩ package=THT]
  S3 = Toggle Switch [package=THT]
  JACK1 = 2.1mm DC Barrel Jack
  R2 = Resistor [tolerance=±5% resistance=1000 package="0603 [SMD]"]
  D1 = Diode [package=diode-1n4148]
  A3 = DYS BE1806
  VCC1 = Battery  # not connected

nets:
  N1: A2.Pin_1, D1.C
  N2: A2.Pin_2, A2.Pin_33, OLED2.GND, S2.Pin_1, S2.Pin_2, R1.leg2
  N3: A2.Pin_3, R1.leg1
  N4: A2.Pin_7, R1.wiper
  N5: A2.Pin_8, S2.Pin_3, S2.Pin_4
  N6: A2.Pin_15, S1.Pin_3, S1.Pin_4
  N7: A2.Pin_16, Part1.SCL
  N8: A2.Pin_17, Part1.SDA
  N9: A2.Pin_23, A3.Pin_1
  N10: Part1.VIN-, A3.Pin_3
  N11: Part1.VIN+, S3.L1
  N12: Part1.VCC, R2.Pin_0, D1.A
  N13: Part1.GND, S1.Pin_1, S1.Pin_2, JACK1.sleeve, A3.Pin_2
  N14: OLED2.VDD, R2.Pin_1
  N15: S3.L2, JACK1.center

notes:
  Motor with ESC

custom parts:
  Waveshare rp2040-zero tht extra conns: .RP2040-Zero, A Low-Cost, High-Performance Pico-Like MCU Board Based On Raspberry Pi Microcontroller RP2040. This varant is THT with the extra connections.
  INA219 High Side DC Current Sensor Breakout: This breakout board will solve all your power-monitoring problems. Instead of struggling with two multimeters, you can just use the handy INA219B chip on this breakout to both measure both the high side voltage and DC current draw over I2C with 1% precision. Most current-measuring devices such as our current panel meter are only good for low side measuring. That means that unless you want to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
  SBX DSUN: SBX DSUN input voltage 4.5 - 28V DC output voltage .8v to 20VDC (step down converter) Output current 3A max
  OLED 128x64 I2C Monochrome Display VDD-GND: OLED 128x64 I2C Monochrome Display. Note: there are two variants of this part, this one is the VDD GND SCK SDA variant. The other is GND VDD SCK SDA. Make sure you select the part that matches your module as using the incorrect part will probably destroy your module! In addition the mounting holes are marked on silkscreen but not by default drilled. If you want drilled mounting holes, copy a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
  2.1mm DC Barrel Jack: 2.1mm DC Barrel Jack with Thru-Hole Connectors (breadboardable) (Mar 2019: replaced pads with standard pads with 0.042 in hole rather than the current 0.030 hole which is too small to mount the part)
  DYS BE1806: quadcopter brushless motor.
  Battery: Your standard 3x 18650 battery pack (11.1 Volts)
